# Fritzing sketch Console 1 - Console 2 (saved by Fritzing 0.9.3b)
breadboards: 1

parts:
  Console_1 = Arduino Uno (Rev3)
  Console_2 = Arduino Uno (Rev3)
  LED1 = LED - 5mm [color="Green (570nm)" package="5 mm [THT]"]
  LED2 = LED - 5mm [color="Blue (525nm)" package="5 mm [THT]"]
  LED3 = LED - 5mm [color="Red (633nm)" package="5 mm [THT]"]
  LED4 = LED - 5mm [color="Red (633nm)" package="5 mm [THT]"]
  LED5 = LED - 5mm [color="Green (570nm)" package="5 mm [THT]"]
  RHT1 = Humidity and Temperature Sensor RHT03
  Grove1 = Grove Temperature Sensor  # not connected
  U1 = V_REG_LD1117VXX [package=78xxl]
  U2 = ESP8266 WiFi Module [part_number=ESP8266]
  R1 = Resistor [tolerance=±5% resistance=220 package="2010 [SMD]"]
  R2 = Resistor [tolerance=±5% resistance=220 package="2010 [SMD]"]
  R3 = Resistor [tolerance=±5% resistance=220 package="2010 [SMD]"]
  R4 = Resistor [tolerance=±5% resistance=220 package="2010 [SMD]"]
  R5 = Resistor [tolerance=±5% resistance=220 package="2010 [SMD]"]

nets:
  N1: Console_1.D8, RHT1.GND_1
  N2: Console_1.D9_PWM, LED2.anode
  N3: Console_1.GND, LED1.cathode, LED2.cathode, LED3.cathode, RHT1.GND_2, R1.Pin_0, R1.Pin_1, R2.Pin_0, R2.Pin_1, R3.Pin_0, R3.Pin_1
  N4: Console_1.D0/RX, Console_2.D1/TX
  N5: Console_1.D1/TX, Console_2.D0/RX
  N6: Console_1.D6_PWM, LED1.anode
  N7: Console_1.D7, LED3.anode
  5V: Console_1.5V, RHT1.Vcc
  N8: Console_2.D8, LED4.anode
  N9: Console_2.D9_PWM, LED5.anode
  GND: Console_2.GND, Console_2.D2, LED4.cathode, LED5.cathode, U1.GND, U2.RXD, U2.GPIO_0, U2.GPIO_2, U2.GND, R4.Pin_0, R4.Pin_1, R5.Pin_0, R5.Pin_1
  N10: Console_2.D3_PWM, U1.OUT, U2.VCC, U2.RST, U2.CH_PD, U2.TXD
  N11: Console_2.5V, U1.IN

custom parts:
  ESP8266 WiFi Module: Generic WiFi Module based on the ESP8266 with onboard PCB antenna and UART communications
