# Fritzing sketch Console 3 (saved by Fritzing 0.9.3b)

parts:
  WeMos_D1_R2 = WeMos D1 R2
  U1 = ESP8266 WiFi Module [part_number=ESP8266]
  U2 = V_REG_LD1117VXX [package=78xxl]
  LED1 = LED - 5mm [color="Red (633nm)" package="5 mm [THT]"]
  LED2 = LED - 5mm [color="Green (570nm)" package="5 mm [THT]"]
  R1 = Resistor [tolerance=±5% resistance=220 package="2010 [SMD]"]
  R2 = Resistor [tolerance=±5% resistance=220 package="2010 [SMD]"]

nets:
  N1: WeMos_D1_R2.D0/RX, U1.RXD
  N2: WeMos_D1_R2.(D5), LED1.anode
  N3: WeMos_D1_R2.(D6), LED2.anode
  N4: WeMos_D1_R2.(D7), U1.TXD
  N5: WeMos_D1_R2.GND#15, U2.GND
  N6: WeMos_D1_R2.GND#20, LED2.cathode, R2.Pin_1
  N7: WeMos_D1_R2.GND#21, R1.Pin_1
  N8: WeMos_D1_R2.5V, U2.IN
  N9: U1.VCC, U2.OUT

custom parts:
  WeMos D1 R2: The D1 R2 is a mini wifi board based on the ESP-8266EX.
  ESP8266 WiFi Module: Generic WiFi Module based on the ESP8266 with onboard PCB antenna and UART communications
